// Logisim project A1_Group2.circ as structural Verilog: 1 circuit, main circuit main
module main (
  input  [3:0] A,
  input  [3:0] B,
  input  [2:0] cs2_cs1_cs0,
  output [3:0] A_2,
  output C,
  output S,
  output V,
  output Z
);

  wire n7404_1_p3, n7404_1_p5, n7404_1_p7, n7404_1_p11, n7404_1_p13, n7404_1_p15, n7408_1_p3, n7408_1_p7,
       n7408_1_p10, n7408_2_p3, n7408_2_p6, n7408_2_p11, n7408_2_p14, n7408_3_p3, n7408_3_p5, n7408_3_p6,
       n7408_3_p10, n7408_3_p11, n7408_3_p13, n7408_3_p14, n7432_1_p3, n7432_1_p6, n7432_1_p11, n7432_1_p14,
       n7432_2_p3, n7432_2_p6, n7432_2_p10, n7432_2_p13, n7432_3_p12, n7432_3_p15, n7432_4_p4, n7432_4_p7,
       n7432_4_p9, n7483_1_p2, n7483_1_p11;

  // _7404 7404_1: pin names not known; wires that end beside it: cs2_cs1_cs0[1], cs2_cs1_cs0[0], n7404_1_p3, B[0], n7404_1_p5, B[1], n7404_1_p7, 1'b0, 1'b1, cs2_cs1_cs0[2], n7404_1_p11, B[3], n7404_1_p13, B[2], n7404_1_p15
  // _7408 7408_1: pin names not known; wires that end beside it: n7404_1_p3, cs2_cs1_cs0[2], n7408_1_p3, 1'b0, 1'b1, n7404_1_p11, n7408_1_p7, C, n7404_1_p11, n7408_1_p10, V
  // _7408 7408_2: pin names not known; wires that end beside it: n7408_1_p3, n7404_1_p5, n7408_2_p3, n7408_1_p3, n7404_1_p7, n7408_2_p6, 1'b0, 1'b1, n7408_1_p3, n7404_1_p13, n7408_2_p11, n7408_1_p3, n7404_1_p15, n7408_2_p14
  // _7432 7432_1: pin names not known; wires that end beside it: n7408_2_p3, A[0], n7432_1_p3, n7408_2_p6, A[1], n7432_1_p6, 1'b0, 1'b1, n7408_2_p11, A[3], n7432_1_p11, n7408_2_p14, A[2], n7432_1_p14
  // _7432 7432_2: pin names not known; wires that end beside it: cs2_cs1_cs0[0], B[0], n7432_2_p3, cs2_cs1_cs0[0], B[1], n7432_2_p6, 1'b1, cs2_cs1_cs0[0], B[3], n7432_2_p10, B[2], cs2_cs1_cs0[0], n7432_2_p13
  // _7408 7408_3: pin names not known; wires that end beside it: n7404_1_p11, cs2_cs1_cs0[1], n7408_3_p3, n7404_1_p11, n7408_3_p5, n7408_3_p6, 1'b0, 1'b1, n7404_1_p11, n7408_3_p10, n7408_3_p11, n7404_1_p11, n7408_3_p13, n7408_3_p14
  // _7483 7483_1: pin names not known; wires that end beside it: n7432_1_p6, n7483_1_p2, n7483_1_p2, 1'b1, n7408_3_p5, 1'b0, 1'b0, n7432_2_p6, A_2[1], n7408_3_p13, n7483_1_p11, 1'b0, n7432_2_p3, n7432_1_p3, A_2[0]
  // _7432 7432_3: pin names not known; wires that end beside it: n7483_1_p2, n7408_3_p3, n7408_1_p3, n7483_1_p11, n7408_3_p6, n7408_1_p3, n7483_1_p2, 1'b0, 1'b1, n7408_3_p11, n7408_1_p3, n7432_3_p12, n7408_1_p3, n7408_3_p14, n7432_3_p15, n7408_3_p14
  // _7483 7483_2: pin names not known; wires that end beside it: n7432_1_p11, n7432_3_p12, n7432_3_p12, 1'b1, n7408_3_p10, 1'b0, 1'b0, n7432_2_p10, A_2[3], n7408_1_p7, n7432_3_p15, 1'b0, n7432_2_p13, n7432_1_p14, A_2[2]
  // _7486 7486_1: pin names not known; wires that end beside it: n7408_1_p7, n7432_3_p12, n7408_1_p10, 1'b1
  // _7404 7404_2: pin names not known; wires that end beside it: 1'b1
  // _7432 7432_4: pin names not known; wires that end beside it: 1'b0, A_2[0], A_2[1], n7432_4_p4, n7432_4_p4, A_2[2], n7432_4_p7, 1'b0, n7432_4_p9, Z, 1'b1, n7432_4_p7, A_2[3], n7432_4_p9

  assign S = A_2[3];

  // Notes on the sheet:
  //   cs2 ~cs0 ~Bi
  //   Ai + cs2 ~cs0 ~Bi
  //   xi
  //   Zi
  //   Yi
  //   cs0 + Bi
  //   ~Cs2 Ci
  //   ~cs2 Ci + Cs2 ~Cs0
endmodule
