// Logisim project 1805008.circ as structural Verilog
module normalizer (
  input  [31:0] in_1,
  input  [9:0] in_2,
  output [31:0] out_3,
  output [9:0] out_4
);

  wire [4:0] bit_extender_2_out, bitfinder_1_index;
  wire [9:0] bit_extender_1_out, multiplexer_1_out;
  wire [30:0] reversebit_1_reversed_output;
  wire [31:0] shifter_1_out, shifter_2_out;

  assign bit_extender_1_out = {{9{in_1[31]}}, in_1[31]};  // Bit_Extender bit_extender_1
  Multiplexer #(.width(10)) multiplexer_1 (
    .in0({{5{1'b0}}, bitfinder_1_index}), .in1(bit_extender_1_out), .out(multiplexer_1_out), .sel(in_1[31]));  // open: en
  assign bit_extender_2_out = {{4{1'b0}}, in_1[31]};  // Bit_Extender bit_extender_2
  Subtractor #(.width(10)) subtractor_1 (.a(in_2), .b(multiplexer_1_out), .out(out_4), .bin(1'b0));  // open: bout
  Shifter #(.width(32), .shift("lr")) shifter_1 (.in(in_1), .\dist (bit_extender_2_out), .out(shifter_1_out));
  reverseBit reversebit_1 (.Input(in_1[30:0]), .Reversed_output(reversebit_1_reversed_output));
  BitFinder #(.width(31)) bitfinder_1 (.in(reversebit_1_reversed_output), .index(bitfinder_1_index));  // open: found
  Shifter #(.width(32)) shifter_2 (.in(in_1), .\dist (bitfinder_1_index), .out(shifter_2_out));
  Multiplexer #(.width(32)) multiplexer_2 (
    .in0(shifter_2_out), .in1(shifter_1_out), .out(out_3), .sel(in_1[31]));  // open: en
endmodule

module reverseBit (
  input  [30:0] Input,
  output [30:0] Reversed_output
);


  assign Reversed_output = {Input[0], Input[1], Input[2], Input[3], Input[4], Input[5], Input[6], Input[7], Input[8], Input[9], Input[10], Input[11], Input[12], Input[13], Input[14], Input[15], Input[16], Input[17], Input[18], Input[19], Input[20], Input[21], Input[22], Input[23], Input[24], Input[25], Input[26], Input[27], Input[28], Input[29], Input[30]};
endmodule
