// Logisim project 1805010(2).circ as structural Verilog: 2 circuits, main circuit main
module main (
  input  [9:0] Exp,
  input  [31:0] Significand,
  output [9:0] Exp_2,
  output [21:0] Significand_2
);

  rounder rounder_1 (.ExpoIn(Exp), .SigIn(Significand), .ExpoOut(Exp_2), .SigOut(Significand_2));
endmodule

module rounder (
  input  [9:0] ExpoIn,
  input  [31:0] SigIn,
  output [9:0] ExpoOut,
  output [21:0] SigOut
);

  wire n7408_1_p3, n7432_1_p3, n7432_1_p5, n7432_1_p6;
  wire [4:0] bit_extender_1_out;
  wire [22:0] adder_2_out;
  wire [22:22] shifter_1_out;

  Adder #(.width(10)) adder_1 (.a(ExpoIn), .b({10{1'b0}}), .out(ExpoOut), .cin(adder_2_out[22]));  // open: cout
  // _7432 7432_1: pin names not known; wires that end beside it: SigIn[9], SigIn[7], n7432_1_p3, n7432_1_p3, n7432_1_p5, n7432_1_p6
  Adder #(.width(23)) adder_2 (.a(SigIn[31:9]), .b({23{1'b0}}), .out(adder_2_out), .cin(n7408_1_p3));  // open: cout
  BitFinder #(.width(7)) bitfinder_1 (.in(SigIn[6:0]), .found(n7432_1_p5));  // open: index
  assign bit_extender_1_out = {{4{1'b0}}, adder_2_out[22]};  // Bit_Extender bit_extender_1
  // _7408 7408_1: pin names not known; wires that end beside it: n7432_1_p6, SigIn[8], n7408_1_p3
  Shifter #(.width(23), .shift("lr")) shifter_1 (
    .in(adder_2_out), .\dist (bit_extender_1_out), .out({shifter_1_out[22], SigOut}));

  // Notes on the sheet:
  //   S = 0-6, R = 7, G = 8, C D FRAC = 31-9
  //   K
  //   C
  //   S
  //   G(R+S+K)
  //   D,FRAC = 21,20-0
endmodule
