// Logisim project 1805010.circ as structural Verilog
module rounder (
  input  [31:0] NormIn
);

  wire n7408_1_p3, n7432_1_p3, n7432_1_p5, n7432_1_p6;
  wire [22:0] adder_1_out;
  wire [31:0] bit_extender_1_out, shifter_1_out;

  // _7432 7432_1: pin names not known; wires that end beside it: NormIn[9], NormIn[7], n7432_1_p3, n7432_1_p3, n7432_1_p5, n7432_1_p6
  Adder #(.width(23)) adder_1 (.a(NormIn[31:9]), .b({23{1'b0}}), .out(adder_1_out), .cin(n7408_1_p3));  // open: cout
  BitFinder #(.width(7)) bitfinder_1 (.in(NormIn[6:0]), .found(n7432_1_p5));  // open: index
  assign bit_extender_1_out = {{9{1'b0}}, adder_1_out};  // Bit_Extender bit_extender_1
  // _7408 7408_1: pin names not known; wires that end beside it: n7432_1_p6, NormIn[8], n7408_1_p3
  Shifter #(.width(32)) shifter_1 (.in(bit_extender_1_out), .\dist (5'b01001), .out(shifter_1_out));
  // Probe on shifter_1_out

  // Notes on the sheet:
  //   S = 0-6, R = 7, G = 8, C D FRAC = 31-9
  //   K
  //   S
  //   G(R+S+K)
endmodule
