// Logisim project 4bitALU.circ as structural Verilog: 4 circuits, main circuit main
module main (
  input  [2:0] s2_s1_s0,
  input  [3:0] A,
  input  [3:0] B,
  output [3:0] A_2,
  output zero
);

  wire or_1_out;
  wire [3:0] adder_1_out, And_out_3, multiplexer_1_out, multiplexer_2_out, n4bitnor_1_out_3, Or_2_out_3,
       shifter_1_out, shifter_2_out, subtractor_1_out;
  wire [3:3] comparator_1_lt, not_1_out;

  not not_1 (not_1_out[3], or_1_out);
  or or_1 (or_1_out, B[2], B[3]);
  _4bitAnd And (.A(A), .B(B), .out_3(And_out_3));
  _4bitiOr Or_2 (.A(A), .B(B), .out_3(Or_2_out_3));
  Adder #(.width(4)) adder_1 (.a(A), .b(B), .out(adder_1_out));  // open: cin, cout
  Subtractor #(.width(4)) subtractor_1 (.a(A), .b(B), .out(subtractor_1_out));  // open: bin, bout
  _4bitNor u_4bitnor_1 (.A(A), .B(B), .out_3(n4bitnor_1_out_3));
  Comparator #(.width(4), .mode("unsigned")) comparator_1 (.a(A), .b(B), .lt(comparator_1_lt[3]));  // open: gt, eq
  Shifter #(.width(4)) shifter_1 (.in(A), .\dist (B[1:0]), .out(shifter_1_out));
  Shifter #(.width(4), .shift("lr")) shifter_2 (.in(A), .\dist (B[1:0]), .out(shifter_2_out));
  Multiplexer #(.width(4), .enable("false")) multiplexer_1 (
    .in0(shifter_1_out), .in1({4{not_1_out[3]}}), .out(multiplexer_1_out), .sel(or_1_out));
  Multiplexer #(.width(4), .enable("false")) multiplexer_2 (
    .in0(shifter_2_out), .in1({4{not_1_out[3]}}), .out(multiplexer_2_out), .sel(or_1_out));
  Multiplexer #(.select(3), .width(4)) multiplexer_3 (
    .in0(And_out_3), .in1(Or_2_out_3), .in2(adder_1_out), .in3(subtractor_1_out), .in4(n4bitnor_1_out_3),
    .in5({4{comparator_1_lt[3]}}), .in6(multiplexer_1_out), .in7(multiplexer_2_out), .out(A_2), .sel(s2_s1_s0));  // open: en
  nor nor_1 (zero, A_2[0], A_2[1], A_2[2], A_2[3]);

  // Notes on the sheet:
  //   slt
  //   sll
  //   srl
endmodule

module _4bitAnd (
  input  [3:0] A,
  input  [3:0] B,
  output [3:0] out_3
);

  and and_1 (out_3[0], A[0], B[0]);
  and and_2 (out_3[1], A[1], B[1]);
  and and_3 (out_3[2], A[2], B[2]);
  and and_4 (out_3[3], A[3], B[3]);
endmodule

module _4bitiOr (
  input  [3:0] A,
  input  [3:0] B,
  output [3:0] out_3
);

  or or_1 (out_3[0], A[0], B[0]);
  or or_2 (out_3[1], A[1], B[1]);
  or or_3 (out_3[2], A[2], B[2]);
  or or_4 (out_3[3], A[3], B[3]);
endmodule

// Nor
module _4bitNor (
  input  [3:0] A,
  input  [3:0] B,
  output [3:0] out_3
);

  nor nor_1 (out_3[0], A[0], B[0]);
  nor nor_2 (out_3[1], A[1], B[1]);
  nor nor_3 (out_3[2], A[2], B[2]);
  nor nor_4 (out_3[3], A[3], B[3]);
endmodule
