// Logisim project control_unit.circ as structural Verilog: 1 circuit, main circuit main
module main (
  input  [3:0] OpCode,
  output Jump,
  output [2:0] ALUop,
  output Bneq,
  output Branch,
  output MemWrite,
  output MemRead,
  output RegWrite,
  output MemToReg,
  output ALUsrc,
  output RegDst
);

  ROM #(.addrWidth(4), .dataWidth(12)) rom_1 (
    .addr(OpCode), .data({RegDst, ALUsrc, MemToReg, RegWrite, MemRead, MemWrite, Branch, Bneq, ALUop, Jump}));  // open: sel

  // Notes on the sheet:
  //   contents of rom_1 (hex, n*v repeats v):
  //   90c 784 500 506 504 900 904 502 444 1 26 902 36 908 906 90e
endmodule
